# Fritzing sketch Sketch (saved by Fritzing 0.9.3b)
perfboards: 1

parts:
  M1 = DC Motor  # not connected
  M2 = DC Motor  # not connected
  U4 = LuaNode32 / ESP32 [part_number=ESP32S-PIN30]
  IC2 = L293D [package=THT]
  U5 = Voltage Regulator - 5V [package="TO220 [THT]"]
  C4 = Electrolytic Capacitor [capacitance=0.22mF package="100 mil [THT, electrolytic]"]
  C5 = Ceramic Capacitor [capacitance=100nF package="100 mil [THT, multilayer]"]
  C6 = Ceramic Capacitor [capacitance=100nF package="100 mil [THT, multilayer]"]
  R1 = Resistor [tolerance=±2% resistance=6.8k package="1206 [SMD]"]
  R2 = Resistor [tolerance=±2% resistance=100 package="1206 [SMD]"]
  R3 = Resistor [tolerance=±2% resistance=100 package="1206 [SMD]"]
  R4 = Resistor [tolerance=±2% resistance=6.8k package="1206 [SMD]"]
  R5 = Resistor [tolerance=±2% resistance=6.8k package="1206 [SMD]"]
  R6 = Resistor [tolerance=±2% resistance=6.8k package="1206 [SMD]"]

nets:
  N1: U4.D32, R6.Pin_0
  N2: U4.D33, R4.Pin_0
  N3: U4.D27, IC2.In_2
  N4: U4.D14, IC2.In_1
  N5: U4.D13, IC2.Enable_1
  GND: U4.GND, IC2.0V, U5.GND, C4.-
  N6: U4.Vin, IC2.+Vmotor, IC2.+V, U5.output_voltage, C4.+
  N7: U4.3V3, R2.Pin_1, R3.Pin_0
  N8: U4.D2, IC2.In_4
  N9: U4.D22, R5.Pin_1
  N10: U4.D23, R1.Pin_1
  N11: IC2.Out_1_(_Controlled_by_Enable_1_), C6.0
  N12: IC2.Out_2_(_Controlled_by_Enable_1_), C6.1
  N13: IC2.Out_4_(_Controlled_by_Enable_2_), C5.1

notes:
  6wires for sensor IO
  6wires for HOA902-11 sensor IO
  white: speed (sensor out)
  blue: anode (LED)
  red: VCC 4.5-5.5V
  yellow: cathode (LED)
  black: GND
  brown: direction (sensor out)

custom parts:
  LuaNode32 / ESP32: New Image for LuaNode32 DOIT ESP32 DEVKIT V1. Base parts from LuaNode32 / ESP32 ESP32 based LuaNode32 by G.Noorlander DOIT Esp32 DevKit v1 (30 pins long, 11 pins width) by Werner Rothschopf (modified by vanepp Dec 2018)
